// Logisim project ex1.circ as structural Verilog: 5 circuits, main circuit NAND1
module NAND1 (
  input  A,
  input  B,
  output RESULT
);

  wire and_1_out;

  and and_1 (and_1_out, A, B);
  not not_1 (RESULT, and_1_out);

  // Notes on the sheet:
  //   PUT CIRCUITRY HERE
endmodule

module NOR1 (
  input  A,
  input  B,
  output RESULT
);

  wire or_1_out;

  or or_1 (or_1_out, A, B);
  not not_1 (RESULT, or_1_out);

  // Notes on the sheet:
  //   PUT CIRCUITRY HERE
endmodule

module XOR1 (
  input  A,
  input  B,
  output RESULT
);

  wire nand1_1_result, nand1_2_result, nand1_3_result;

  NAND1 nand1_1 (.A(A), .B(B), .RESULT(nand1_1_result));
  NAND1 nand1_2 (.A(A), .B(nand1_1_result), .RESULT(nand1_2_result));
  NAND1 nand1_3 (.A(nand1_1_result), .B(B), .RESULT(nand1_3_result));
  NAND1 nand1_4 (.A(nand1_2_result), .B(nand1_3_result), .RESULT(RESULT));

  // Notes on the sheet:
  //   PUT CIRCUITRY HERE
endmodule

module MUX2 (
  input  A,
  input  B,
  input  Sel,
  output RESULT
);

  wire nand1_1_result, nand1_2_result, nand1_3_result;

  NAND1 nand1_1 (.A(B), .B(Sel), .RESULT(nand1_1_result));
  NAND1 nand1_2 (.A(Sel), .B(Sel), .RESULT(nand1_2_result));
  NAND1 nand1_3 (.A(A), .B(nand1_2_result), .RESULT(nand1_3_result));
  NAND1 nand1_4 (.A(nand1_1_result), .B(nand1_3_result), .RESULT(RESULT));

  // Notes on the sheet:
  //   PUT CIRCUITRY HERE
endmodule

module MUX4 (
  input  A,
  input  B,
  input  C,
  input  D,
  input  Sel1,
  input  Sel2,
  output RESULT
);

  wire and_1_out, and_2_out, and_3_out, and_4_out, and_5_out, and_6_out, and_7_out, and_8_out, not_1_out,
       not_2_out, not_3_out, not_4_out, or_1_out, or_2_out;

  not not_1 (not_1_out, Sel2);
  not not_2 (not_2_out, Sel1);
  not not_3 (not_3_out, Sel1);
  not not_4 (not_4_out, Sel2);
  and and_1 (and_1_out, Sel1, Sel2);
  and and_2 (and_2_out, Sel1, not_1_out);
  and and_3 (and_3_out, not_2_out, Sel2);
  and and_4 (and_4_out, not_3_out, not_4_out);
  and and_5 (and_5_out, D, and_1_out);
  and and_6 (and_6_out, B, and_2_out);
  or or_1 (or_1_out, and_5_out, and_6_out);
  and and_7 (and_7_out, C, and_3_out);
  or or_2 (or_2_out, or_1_out, and_7_out);
  and and_8 (and_8_out, A, and_4_out);
  or or_3 (RESULT, or_2_out, and_8_out);

  // Notes on the sheet:
  //   PUT CIRCUITRY HERE
endmodule
