// Logisim project cpu.circ as structural Verilog: 1 circuit, main circuit cpu
module cpu (
  input  clk,
  input  [31:0] INSTRUCTION,
  input  [31:0] READ_DATA,
  output [31:0] WRITE_ADDRESS,
  output [31:0] PROGRAM_COUNTER,
  output [31:0] ra,
  output [31:0] sp,
  output [31:0] t0,
  output [31:0] t1,
  output [31:0] t2,
  output [31:0] s0,
  output [31:0] s1,
  output [31:0] a0,
  output [31:0] tohost,
  output [3:0] WRITE_ENABLE,
  output [31:0] WRITE_DATA
);

  wire ASel, BrEq, BrLt, BrUn, BSel, comparator_1_eq, comparator_2_eq, comparator_3_eq, comparator_4_eq,
       comparator_5_eq, comparator_6_eq, comparator_7_eq, CSRSel, CSRWen, isLB, isLH, MemRW, PCSel, RegWEn,
       SB, SH;
  wire [1:0] WBSel;
  wire [2:0] funct3, ImmSel;
  wire [3:0] ALUSel, multiplexer_6_out, multiplexer_7_out;
  wire [6:0] funct7;
  wire [24:0] INSTRUCTION_DECODE;
  wire [31:0] adder_1_out, adder_2_out, bit_extender_1_out, bit_extender_2_out, bit_extender_3_out, gen_imm,
       multiplexer_1_out, multiplexer_2_out, multiplexer_3_out, multiplexer_4_out, multiplexer_5_out,
       multiplexer_10_out, PROGRAM_COUNTER_2, read_data_1, READ_DATA_DECODE, WB_data;

  Adder #(.width(32)) adder_1 (.a(PROGRAM_COUNTER), .b(32'h4), .out(adder_1_out));  // open: cin, cout
  Multiplexer #(.enable("false"), .width(32)) multiplexer_1 (
    .in0(INSTRUCTION), .in1(32'h13), .out(multiplexer_1_out), .sel(PCSel));
  Multiplexer #(.enable("false"), .width(32)) multiplexer_2 (
    .in0(adder_1_out), .in1(WRITE_ADDRESS), .out(multiplexer_2_out), .sel(PCSel));
  Register #(.width(32)) PC (.D(multiplexer_2_out), .clk(clk), .Q(PROGRAM_COUNTER));  // open: en, clr
  Register #(.width(32)) register_1 (.D(PROGRAM_COUNTER), .clk(clk), .Q(PROGRAM_COUNTER_2));  // open: en, clr
  Register #(.width(32)) IF_ID (
    .D(multiplexer_1_out), .clk(clk),
    .Q({funct7, INSTRUCTION_DECODE[24:15], funct3, INSTRUCTION_DECODE[11:0]}));  // open: en, clr
  control_logic control_logic_1 (
    .CSRWen(CSRWen), .PCSel(PCSel), .RegWEn(RegWEn), .ImmSel(ImmSel), .BrUn(BrUn), .ASel(ASel), .BSel(BSel),
    .ALUSel(ALUSel), .MemRW(MemRW), .WBSel(WBSel), .CSRSel(CSRSel),
    .inst({funct7, INSTRUCTION_DECODE[24:15], funct3, INSTRUCTION_DECODE[11:0]}), .BrEq(BrEq), .BrLt(BrLt));
  imm_gen imm_gen_1 (
    .inst({funct7, INSTRUCTION_DECODE[24:15], funct3, INSTRUCTION_DECODE[11:0]}), .ImmSel(ImmSel),
    .imm(gen_imm));
  assign bit_extender_1_out = {{27{INSTRUCTION_DECODE[19]}}, INSTRUCTION_DECODE[19:15]};  // Bit_Extender bit_extender_1
  Multiplexer #(.enable("false"), .width(32)) multiplexer_3 (
    .in0(bit_extender_1_out), .in1(gen_imm), .out(multiplexer_3_out), .sel(CSRSel));
  regfile regfile_1 (
    .rs1(INSTRUCTION_DECODE[19:15]), .rs2(INSTRUCTION_DECODE[24:20]), .rd(INSTRUCTION_DECODE[11:7]),
    .Write_Data(WB_data), .RegWEn(RegWEn), .clk(clk), .ra(ra), .sp(sp), .t0(t0), .t1(t1), .t2(t2), .s0(s0),
    .s1(s1), .a0(a0), .Read_Data_1(read_data_1), .Read_Data_2(WRITE_DATA));
  branch_comp branch_comp_1 (.rs1(read_data_1), .rs2(WRITE_DATA), .BrUn(BrUn), .BrEq(BrEq), .BrLt(BrLt));
  csr csr_1 (.CSR_address(12'h51e), .CSR_din(multiplexer_3_out), .CSR_WE(CSRWen), .clk(clk), .tohost(tohost));
  Multiplexer #(.enable("false"), .width(32)) multiplexer_4 (
    .in0(read_data_1), .in1(PROGRAM_COUNTER_2), .out(multiplexer_4_out), .sel(ASel));
  Multiplexer #(.enable("false"), .width(32)) multiplexer_5 (
    .in0(WRITE_DATA), .in1(gen_imm), .out(multiplexer_5_out), .sel(BSel));
  alu alu_1 (.Result(WRITE_ADDRESS), .A(multiplexer_4_out), .B(multiplexer_5_out), .ALUSel(ALUSel));
  Multiplexer #(.enable("false"), .width(4)) multiplexer_6 (
    .in0(4'b1111), .in1(4'b0011), .out(multiplexer_6_out), .sel(SH));
  Multiplexer #(.enable("false"), .width(4)) multiplexer_7 (
    .in0(multiplexer_6_out), .in1(4'b0001), .out(multiplexer_7_out), .sel(SB));
  Multiplexer #(.enable("false"), .width(4)) multiplexer_8 (
    .in0(4'b0000), .in1(multiplexer_7_out), .out(WRITE_ENABLE), .sel(MemRW));
  Comparator #(.width(3)) comparator_1 (.a(funct3), .b(3'b000), .eq(comparator_1_eq));  // open: gt, lt
  Comparator #(.width(7)) comparator_2 (
    .a(INSTRUCTION_DECODE[6:0]), .b(7'b0100011), .eq(comparator_2_eq));  // open: gt, lt
  Comparator #(.width(3)) comparator_3 (.a(funct3), .b(3'b001), .eq(comparator_3_eq));  // open: gt, lt
  and and_1 (SB, comparator_1_eq, comparator_2_eq);
  and and_2 (SH, comparator_2_eq, comparator_3_eq);
  Comparator #(.width(3)) comparator_4 (.a(funct3), .b(3'b000), .eq(comparator_4_eq));  // open: gt, lt
  Comparator #(.width(7)) comparator_5 (
    .a(INSTRUCTION_DECODE[6:0]), .b(7'b0000011), .eq(comparator_5_eq));  // open: gt, lt
  Comparator #(.width(3)) comparator_6 (.a(funct3), .b(3'b001), .eq(comparator_6_eq));  // open: gt, lt
  Comparator #(.width(7)) comparator_7 (
    .a(INSTRUCTION_DECODE[6:0]), .b(7'b0000011), .eq(comparator_7_eq));  // open: gt, lt
  and and_3 (isLB, comparator_4_eq, comparator_5_eq);
  and and_4 (isLH, comparator_6_eq, comparator_7_eq);
  Multiplexer #(.enable("false"), .select(2), .width(32)) multiplexer_9 (
    .in0(READ_DATA_DECODE), .in1(WRITE_ADDRESS), .in2(adder_2_out), .in3(gen_imm), .out(WB_data), .sel(WBSel));
  Adder #(.width(32)) adder_2 (.a(PROGRAM_COUNTER_2), .b(32'h4), .out(adder_2_out));  // open: cin, cout
  assign bit_extender_2_out = {{24{READ_DATA[7]}}, READ_DATA[7:0]};  // Bit_Extender bit_extender_2
  assign bit_extender_3_out = {{16{READ_DATA[15]}}, READ_DATA[15:0]};  // Bit_Extender bit_extender_3
  Multiplexer #(.enable("false"), .width(32)) multiplexer_10 (
    .in0(READ_DATA), .in1(bit_extender_3_out), .out(multiplexer_10_out), .sel(isLH));
  Multiplexer #(.enable("false"), .width(32)) multiplexer_11 (
    .in0(multiplexer_10_out), .in1(bit_extender_2_out), .out(READ_DATA_DECODE), .sel(isLB));

  // Other names for the same wires on the sheet: alu_result[31:0] = WRITE_ADDRESS;
  //   opcode[6:0] = INSTRUCTION_DECODE[6:0]; rd[4:0] = INSTRUCTION_DECODE[11:7];
  //   INSTRUCTION_DECODE (some bits) = {funct7, funct3}; rs1[4:0] = INSTRUCTION_DECODE[19:15];
  //   rs2[4:0] = INSTRUCTION_DECODE[24:20]; read_data_2[31:0] = WRITE_DATA

  // Notes on the sheet:
  //   Output to IMEM
  //   IMEM (do **NOT** move this)
  //   IF
  //   Inputs from IMEM
  //   Inputs/Outputs for testing. Do **NOT** move these.
  //   ID
  //   EXE
  //   Outputs To DMEM
  //   DMEM (do **NOT** move this)
  //   Inputs From DMEM
  //   MA
  //   WB
endmodule
