// Logisim project mem.circ as structural Verilog: 1 circuit, main circuit mem
module mem (
  input  [31:0] in_1,
  input  [3:0] in_2,
  input  [31:0] in_3,
  input  in_4,
  output [31:0] out_5
);

  RAM #(.addrWidth(14)) ram_1 (
    .addr(in_1[15:2]), .we(in_2[0]), .oe(1'b1), .clk(in_4), .din(in_3[7:0]), .dout(out_5[7:0]));
  RAM #(.addrWidth(14)) ram_2 (
    .addr(in_1[15:2]), .we(in_2[1]), .oe(1'b1), .clk(in_4), .din(in_3[15:8]), .dout(out_5[15:8]));
  RAM #(.addrWidth(14)) ram_3 (
    .addr(in_1[15:2]), .we(in_2[2]), .oe(1'b1), .clk(in_4), .din(in_3[23:16]), .dout(out_5[23:16]));
  RAM #(.addrWidth(14)) ram_4 (
    .addr(in_1[15:2]), .we(in_2[3]), .oe(1'b1), .clk(in_4), .din(in_3[31:24]), .dout(out_5[31:24]));
endmodule
