// Logisim project regfile.circ as structural Verilog: 1 circuit, main circuit regfile
module regfile (
  input  [4:0] rs1,
  input  [4:0] rs2,
  input  [4:0] rd,
  input  [31:0] Write_Data,
  input  RegWEn,
  input  clk,
  input  in_7,
  output [31:0] ra,
  output [31:0] sp,
  output [31:0] t0,
  output [31:0] t1,
  output [31:0] t2,
  output [31:0] s0,
  output [31:0] s1,
  output [31:0] a0,
  output [31:0] Read_Data_1,
  output [31:0] Read_Data_2
);

  wire demultiplexer_1_out17, write_en_and_rd_1, write_en_and_rd_2, write_en_and_rd_3, write_en_and_rd_4,
       write_en_and_rd_5, write_en_and_rd_6, write_en_and_rd_7, write_en_and_rd_8, write_en_and_rd_9,
       write_en_and_rd_10, write_en_and_rd_11, write_en_and_rd_12, write_en_and_rd_13, write_en_and_rd_14,
       write_en_and_rd_15, write_en_and_rd_16, write_en_and_rd_17, write_en_and_rd_18, write_en_and_rd_19,
       write_en_and_rd_20, write_en_and_rd_21, write_en_and_rd_22, write_en_and_rd_23, write_en_and_rd_24,
       write_en_and_rd_25, write_en_and_rd_26, write_en_and_rd_27, write_en_and_rd_28, write_en_and_rd_29,
       write_en_and_rd_30, write_en_and_rd_31;
  wire [31:0] output_x3, output_x4, output_x11, output_x12, output_x13, output_x14, output_x15, output_x16,
       output_x17, output_x18, output_x19, output_x20, output_x21, output_x22, output_x23, output_x24,
       output_x25, output_x26, output_x27, output_x28, output_x29, output_x30, output_x31, x0;

  Register #(.width(32)) x1 (.D(Write_Data), .en(write_en_and_rd_1), .clk(clk), .Q(ra));  // open: clr
  Register #(.width(32)) x5 (.D(Write_Data), .en(write_en_and_rd_5), .clk(clk), .Q(t0));  // open: clr
  Register #(.width(32)) x9 (.D(Write_Data), .en(write_en_and_rd_9), .clk(clk), .Q(s1));  // open: clr
  Register #(.width(32)) x13 (.D(Write_Data), .en(write_en_and_rd_13), .clk(clk), .Q(output_x13));  // open: clr
  Register #(.width(32)) x17 (.D(Write_Data), .en(write_en_and_rd_17), .clk(clk), .Q(output_x17));  // open: clr
  Register #(.width(32)) x21 (.D(Write_Data), .en(write_en_and_rd_21), .clk(clk), .Q(output_x21));  // open: clr
  Register #(.width(32)) x25 (.D(Write_Data), .en(write_en_and_rd_25), .clk(clk), .Q(output_x25));  // open: clr
  Register #(.width(32)) x29 (.D(Write_Data), .en(write_en_and_rd_29), .clk(clk), .Q(output_x29));  // open: clr
  Register #(.width(32)) x2 (.D(Write_Data), .en(write_en_and_rd_2), .clk(clk), .Q(sp));  // open: clr
  Register #(.width(32)) x6 (.D(Write_Data), .en(write_en_and_rd_6), .clk(clk), .Q(t1));  // open: clr
  Register #(.width(32)) x10 (.D(Write_Data), .en(write_en_and_rd_10), .clk(clk), .Q(a0));  // open: clr
  Register #(.width(32)) x14 (.D(Write_Data), .en(write_en_and_rd_14), .clk(clk), .Q(output_x14));  // open: clr
  Register #(.width(32)) x18 (.D(Write_Data), .en(write_en_and_rd_18), .clk(clk), .Q(output_x18));  // open: clr
  Register #(.width(32)) x22 (.D(Write_Data), .en(write_en_and_rd_22), .clk(clk), .Q(output_x22));  // open: clr
  Register #(.width(32)) x26 (.D(Write_Data), .en(write_en_and_rd_26), .clk(clk), .Q(output_x26));  // open: clr
  Register #(.width(32)) x30 (.D(Write_Data), .en(write_en_and_rd_30), .clk(clk), .Q(output_x30));  // open: clr
  Register #(.width(32)) x3 (.D(Write_Data), .en(write_en_and_rd_3), .clk(clk), .Q(output_x3));  // open: clr
  Register #(.width(32)) x7 (.D(Write_Data), .en(write_en_and_rd_7), .clk(clk), .Q(t2));  // open: clr
  Register #(.width(32)) x11 (.D(Write_Data), .en(write_en_and_rd_11), .clk(clk), .Q(output_x11));  // open: clr
  Register #(.width(32)) x15 (.D(Write_Data), .en(write_en_and_rd_15), .clk(clk), .Q(output_x15));  // open: clr
  Register #(.width(32)) x19 (.D(Write_Data), .en(write_en_and_rd_19), .clk(clk), .Q(output_x19));  // open: clr
  Register #(.width(32)) x23 (.D(Write_Data), .en(write_en_and_rd_23), .clk(clk), .Q(output_x23));  // open: clr
  Register #(.width(32)) x27 (.D(Write_Data), .en(write_en_and_rd_27), .clk(clk), .Q(output_x27));  // open: clr
  Register #(.width(32)) x31 (.D(Write_Data), .en(write_en_and_rd_31), .clk(clk), .Q(output_x31));  // open: clr
  Register #(.width(32)) x4 (.D(Write_Data), .en(write_en_and_rd_4), .clk(clk), .Q(output_x4));  // open: clr
  Register #(.width(32)) x8 (.D(Write_Data), .en(write_en_and_rd_8), .clk(clk), .Q(s0));  // open: clr
  Register #(.width(32)) x12 (.D(Write_Data), .en(write_en_and_rd_12), .clk(clk), .Q(output_x12));  // open: clr
  Register #(.width(32)) x16 (.D(Write_Data), .en(write_en_and_rd_16), .clk(clk), .Q(output_x16));  // open: clr
  Register #(.width(32)) x20 (.D(Write_Data), .en(write_en_and_rd_20), .clk(clk), .Q(output_x20));  // open: clr
  Register #(.width(32)) x24 (.D(Write_Data), .en(write_en_and_rd_24), .clk(clk), .Q(output_x24));  // open: clr
  Register #(.width(32)) x28 (.D(Write_Data), .en(write_en_and_rd_28), .clk(clk), .Q(output_x28));  // open: clr
  assign x0 = {{31{in_7}}, in_7};  // Bit_Extender bit_extender_1
  Multiplexer #(.enable("false"), .select(5), .width(32)) multiplexer_1 (
    .in0(x0), .in1(ra), .in2(sp), .in3(output_x3), .in4(output_x4), .in5(t0), .in6(t1), .in7(t2), .in8(s0),
    .in9(s1), .in10(a0), .in11(output_x11), .in12(output_x12), .in13(output_x13), .in14(output_x14),
    .in15(output_x15), .in16(output_x16), .in17(output_x17), .in18(output_x18), .in19(output_x19),
    .in20(output_x20), .in21(output_x21), .in22(output_x22), .in23(output_x23), .in24(output_x24),
    .in25(output_x25), .in26(output_x26), .in27(output_x27), .in28(output_x28), .in29(output_x29),
    .in30(output_x30), .in31(output_x31), .out(Read_Data_1), .sel(rs1));
  Multiplexer #(.enable("false"), .select(5), .width(32)) multiplexer_2 (
    .in0(x0), .in1(ra), .in2(sp), .in3(output_x3), .in4(output_x4), .in5(t0), .in6(t1), .in7(t2), .in8(s0),
    .in9(s1), .in10(a0), .in11(output_x11), .in12(output_x12), .in13(output_x13), .in14(output_x14),
    .in15(output_x15), .in16(output_x16), .in17(output_x17), .in18(output_x18), .in19(output_x19),
    .in20(output_x20), .in21(output_x21), .in22(output_x22), .in23(output_x23), .in24(output_x24),
    .in25(output_x25), .in26(output_x26), .in27(output_x27), .in28(output_x28), .in29(output_x29),
    .in30(output_x30), .in31(output_x31), .out(Read_Data_2), .sel(rs2));
  Demultiplexer #(.enable("false"), .select(5)) demultiplexer_1 (
    .out1(write_en_and_rd_1), .out2(write_en_and_rd_2), .out3(write_en_and_rd_3), .out4(write_en_and_rd_4),
    .out5(write_en_and_rd_5), .out6(write_en_and_rd_6), .out7(write_en_and_rd_7), .out8(write_en_and_rd_8),
    .out9(write_en_and_rd_9), .out10(write_en_and_rd_10), .out11(write_en_and_rd_11),
    .out12(write_en_and_rd_12), .out13(write_en_and_rd_13), .out14(write_en_and_rd_14),
    .out15(write_en_and_rd_15), .out16(write_en_and_rd_16), .out17(demultiplexer_1_out17),
    .out18(write_en_and_rd_18), .out19(write_en_and_rd_19), .out20(write_en_and_rd_20),
    .out21(write_en_and_rd_21), .out22(write_en_and_rd_22), .out23(write_en_and_rd_23),
    .out24(write_en_and_rd_24), .out25(write_en_and_rd_25), .out26(write_en_and_rd_26),
    .out27(write_en_and_rd_27), .out28(write_en_and_rd_28), .out29(write_en_and_rd_29),
    .out30(write_en_and_rd_30), .out31(write_en_and_rd_31), .in(RegWEn), .sel(rd));  // open: out0

  // Other names for the same wires on the sheet: read_data1[31:0] = Read_Data_1; read_data2[31:0] = Read_Data_2;
  //   read_reg1[4:0] = rs1; read_reg2[4:0] = rs2; write_en = RegWEn; write_reg[4:0] = rd

  // Notes on the sheet:
  //   INPUTS to your circuit
  //   DON'T CHANGE THE LOCATIONS OF THE INPUTS AND OUTPUTS!
  //   These are DEBUG/TEST outputs from your circuit.
  //   32 Registers
  //   OUTPUTS from your circuit
  //   Write Data
  //   Read Data
endmodule
